# Fritzing sketch ReedDoorSensor (saved by Fritzing 0.9.3b)
breadboards: 1

parts:
  Part1 = Arduino Micro (Rev3)
  S1 = SWITCH-MOMENTARY-2 [package=tactile-switch-1101ne]

nets:
  N1: Part1.GND, S1.1
  N2: Part1.D3/SCL, S1.2

notes:
  Reed sensor is used to detect open and closed door.
  Pin 3 connected to reed open/ closed connection.
  GND connected to ground connection.
